// Logisim project 3Bits V 01.circ as structural Verilog: 1 circuit, main circuit main
module main (
  input  A,
  input  B,
  input  A_2,
  input  B_2,
  input  A_3,
  input  B_3,
  input  A_4,
  input  B_4
);

  wire and_1_out, and_2_out, and_3_out, and_4_out, and_5_out, and_6_out, and_7_out, and_8_out, and_9_out,
       not_1_out, not_2_out, or_1_out, or_3_out, xor_1_out, xor_2_out, xor_3_out, xor_4_out, xor_5_out;

  not not_1 (not_1_out, B);
  not not_2 (not_2_out, A);
  and and_1 (and_1_out, not_1_out, A);
  and and_2 (and_2_out, B, not_2_out);
  xor xor_1 (xor_1_out, A_2, B_2);
  and and_3 (and_3_out, A_2, or_3_out);
  and and_4 (and_4_out, B_2, A_2);
  and and_5 (and_5_out, or_3_out, B_2);
  LED led_1 (.in(or_1_out));
  or or_1 (or_1_out, and_1_out, and_2_out);
  xor xor_2 (xor_2_out, xor_1_out, or_3_out);
  LED led_2 (.in(xor_2_out));
  // OR_Gate or_2 has open pins: in0=and_3_out, in1=and_4_out, in2=and_5_out, out=open
  xor xor_3 (xor_3_out, A_3, B_3);
  and and_6 (and_6_out, A_3, and_9_out);
  and and_7 (and_7_out, B_3, A_3);
  and and_8 (and_8_out, and_9_out, B_3);
  xor xor_4 (xor_4_out, xor_3_out, and_9_out);
  LED led_3 (.in(xor_4_out));
  or or_3 (or_3_out, and_6_out, and_7_out, and_8_out);
  LED led_4 (.in(xor_5_out));
  xor xor_5 (xor_5_out, B_4, A_4);
  and and_9 (and_9_out, A_4, B_4);
endmodule
